# Fritzing sketch bcg_diagram1 (saved by Fritzing 0.9.6b)
stripboards: 1

parts:
  Q1 = NPN-Transistor [part_number=2N2222 package="TO92 [THT]"]
  R99 = Resistor [tolerance=±5% resistance=1k power=0.25 package=THT]
  D1 = Rectifier Diode [part_number=1N4007 package="300 mil [THT]"]
  230_VAC = Power plug
  Eureka_Mignon_Motor = DC Motor
  DIP = DIP SWITCH [package=dipswitch-02]
  SW_porta = Round Pushbutton
  HX_711 = HX711 Weighing Sensor Module  # not connected
  230_VAC_-->_5VDC = HLK-PM01
  IC1 = Hex Inverter Schmitt Trigger SN74HC14 [package="DIP (Dual Inline)"]
  Part5 = Arduino Micro (Rev3)
  R11 = Resistor [tolerance=±5% resistance=10k package=THT]
  R21 = Resistor [tolerance=±5% resistance=10k package=THT]
  R41 = Resistor [tolerance=±5% resistance=10k package=THT]
  R51 = Resistor [tolerance=±5% resistance=10k package=THT]
  C51 = Ceramic Capacitor [capacitance=10nF voltage=35V package="100 mil [THT, multilayer]"]
  C41 = Ceramic Capacitor [capacitance=10nF voltage=35V package="100 mil [THT, multilayer]"]
  R42 = Resistor [tolerance=±5% resistance=10k package=THT]
  R52 = Resistor [tolerance=±5% resistance=10k package=THT]
  R61 = Resistor [tolerance=±5% resistance=10k package=THT]
  R62 = Resistor [tolerance=±5% resistance=10k package=THT]
  C61 = Ceramic Capacitor [capacitance=10nF voltage=35V package="100 mil [THT, multilayer]"]
  R31 = Resistor [tolerance=±5% resistance=10k package=THT]
  C31 = Ceramic Capacitor [capacitance=10nF voltage=35V package="100 mil [THT, multilayer]"]
  R32 = Resistor [tolerance=±5% resistance=10k package=THT]
  GR2L-1A-E = Omron_G2RL-1A-E [part_number=G2RL-1A-E]
  ENCODER = encoder_v2

nets (from the breadboard view):
  GND: Q1.E, DIP.1, DIP.2, SW_porta.leg0, 230_VAC_-->_5VDC.-Vo, IC1.GND, IC1.5A, IC1.6A, Part5.GND, C51.1, C41.0, C61.0, C31.1, ENCODER.connector2, ENCODER.connector4
  N1: Q1.B, R99.Pin_0
  N2: Q1.C, D1.anode, GR2L-1A-E.connector0
  N3: R99.Pin_1, Part5.D10_PWM/A10
  N4: D1.cathode, 230_VAC_-->_5VDC.+Vo, Part5.VIN, GR2L-1A-E.connector6
  N5: 230_VAC.GND, 230_VAC_-->_5VDC.AC#1, GR2L-1A-E.connector1, GR2L-1A-E.connector2
  N6: 230_VAC.VCC, Eureka_Mignon_Motor.pin_1, 230_VAC_-->_5VDC.AC#0
  N7: Eureka_Mignon_Motor.pin_2, GR2L-1A-E.connector4
  N8: DIP.3, Part5.D9_PWM/A9, R21.Pin_1
  N9: DIP.4, Part5.D8_PWM/A8, R11.Pin_1
  N10: SW_porta.leg1, R31.Pin_1, R32.Pin_0
  N11: IC1.1A, C41.1, R42.Pin_1
  N12: IC1.1Y, Part5.D4_PWM/A6
  N13: IC1.2A, C51.0, R52.Pin_1
  N14: IC1.2Y, Part5.D5_PWM
  N15: IC1.3A, R62.Pin_1, C61.1
  N16: IC1.3Y, Part5.D6_PWM/A7
  N17: IC1.4Y, Part5.D7
  N18: IC1.4A, C31.0, R32.Pin_1
  VCC: IC1.VCC, Part5.3V3, R11.Pin_0, R21.Pin_0, R41.Pin_0, R51.Pin_0, R61.Pin_0, R31.Pin_0
  N19: R41.Pin_1, R42.Pin_0, ENCODER.connector1
  N20: R51.Pin_1, R52.Pin_0, ENCODER.connector3
  N21: R61.Pin_1, R62.Pin_0, ENCODER.connector5

notes:
  Better Coffee Grinder
  draft for MC-internal pull-up & debounce
  v 0.2
